// Logisim project CPU.circ as structural Verilog: 3 circuits, main circuit main
module main (
  input  Reset,
  input  Aktive
);

  wire cpu_1_write, mainbord_1_cpu_reset, mainbord_1_cpu_takt, mainbord_1_ram_aktive, mainbord_1_ram_lesen,
       \mainbord_1_ram_löschen , mainbord_1_ram_schreibe, mainbord_1_ram_takt;
  wire [7:0] cpu_1_adresse, cpu_1_output, mainbord_1_cpu_input, mainbord_1_ram_adresse, mainbord_1_ram_input,
       ram_1_data;

  CPU cpu_1 (
    .Input(mainbord_1_cpu_input), .Reset(mainbord_1_cpu_reset), .Takt(mainbord_1_cpu_takt),
    .Adresse(cpu_1_adresse), .Output(cpu_1_output), .Write(cpu_1_write));
  Mainbord mainbord_1 (
    .Reset(Reset), .Aktive(Aktive), .Ram_Takt(mainbord_1_ram_takt), .Ram_Schreibe(mainbord_1_ram_schreibe),
    .Ram_Input(mainbord_1_ram_input), .Ram_Output(ram_1_data), .Ram_Adresse(mainbord_1_ram_adresse),
    .CPU_Takt(mainbord_1_cpu_takt), .CPU_Input(mainbord_1_cpu_input), .CPU_Adresse(cpu_1_adresse),
    .CPU_Output(cpu_1_output), .CPU_Write(cpu_1_write), .Ram_Aktive(mainbord_1_ram_aktive),
    .Ram_Lesen(mainbord_1_ram_lesen), .\Ram_Löschen (\mainbord_1_ram_löschen ),
    .CPU_Reset(mainbord_1_cpu_reset));
  RAM #(.bus("separate")) ram_1 (
    .addr(mainbord_1_ram_adresse), .din(mainbord_1_ram_input), .data(ram_1_data),
    .str(mainbord_1_ram_schreibe), .sel(mainbord_1_ram_aktive), .clk(mainbord_1_ram_takt),
    .ld(mainbord_1_ram_lesen), .clr(\mainbord_1_ram_löschen ));
  // DotMatrix #(.inputtype("select"), .matrixcols(12), .matrixrows(12)) dotmatrix_1: pin names not known
endmodule

module CPU (
  input  [7:0] Input,
  input  Reset,
  input  Takt,
  output [7:0] Adresse,
  output [7:0] Output,
  output Write
);

  wire and_1_out, and_2_out, and_4_out, and_5_out, and_6_out, and_7_out, and_8_out, and_9_out, and_10_out,
       and_11_out, and_12_out, and_13_out, and_14_out, and_15_out, and_16_out, and_17_out, and_18_out,
       and_19_out, and_20_out, and_21_out, and_22_out, and_23_out, Aufgabe, comparator_1_eq, comparator_2_eq,
       comparator_3_eq, comparator_4_eq, comparator_5_eq, comparator_6_eq, comparator_7_eq, comparator_8_eq,
       comparator_9_eq, comparator_10_eq, comparator_11_eq, comparator_12_eq, comparator_13_eq,
       comparator_14_eq, comparator_15_eq, comparator_16_eq, comparator_17_eq, comparator_18_eq,
       comparator_19_eq, comparator_20_eq, comparator_21_eq, comparator_21_gt, comparator_21_lt,
       comparator_22_eq, comparator_22_gt, comparator_22_lt, counter_1_carry, Jump, nor_1_out, not_1_out,
       not_2_out, or_1_out, or_2_out, or_3_out, or_4_out, or_5_out, or_6_out, or_7_out, or_8_out, or_9_out,
       or_10_out, or_11_out, or_12_out, or_13_out, or_14_out;
  wire [0:0] counter_1_q;
  wire [7:0] adder_1_out, Atribut, counter_2_q, divider_1_out, Input_Speicher, multiplier_1_out,
       register_1_q, Speicher_A, Speicher_B, subtractor_1_out;

  Counter #(.width(2), .max('h2), .trigger("falling")) counter_1 (
    .Q({Aufgabe, counter_1_q[0]}), .carry(counter_1_carry), .clk(Takt), .clr(or_2_out));  // open: load, D, count
  Register #(.trigger("falling")) register_1 (.D(Input), .Q(register_1_q), .clk(and_1_out), .clr(Reset));  // open: en
  and and_1 (and_1_out, ~Aufgabe, ~counter_1_q[0]);  // AND_Gate
  not not_1 (not_1_out, Jump);
  or or_1 (or_1_out, Jump, ~counter_1_carry);  // OR_Gate
  and and_2 (and_2_out, or_1_out, Takt);
  Comparator comparator_1 (.a(register_1_q), .b(8'h1), .eq(comparator_1_eq));  // open: gt, lt
  Comparator comparator_2 (.a(register_1_q), .b(8'h2), .eq(comparator_2_eq));  // open: gt, lt
  Comparator comparator_3 (.a(register_1_q), .b(8'h3), .eq(comparator_3_eq));  // open: gt, lt
  Comparator comparator_4 (.a(register_1_q), .b(8'h4), .eq(comparator_4_eq));  // open: gt, lt
  Comparator comparator_5 (.a(register_1_q), .b(8'h5), .eq(comparator_5_eq));  // open: gt, lt
  Comparator comparator_6 (.a(register_1_q), .b(8'h6), .eq(comparator_6_eq));  // open: gt, lt
  Comparator comparator_7 (.a(register_1_q), .b(8'h7), .eq(comparator_7_eq));  // open: gt, lt
  Comparator comparator_8 (.a(register_1_q), .b(8'h8), .eq(comparator_8_eq));  // open: gt, lt
  Comparator comparator_9 (.a(register_1_q), .b(8'h9), .eq(comparator_9_eq));  // open: gt, lt
  Comparator comparator_10 (.a(register_1_q), .b(8'ha), .eq(comparator_10_eq));  // open: gt, lt
  Comparator comparator_11 (.a(register_1_q), .b(8'hb), .eq(comparator_11_eq));  // open: gt, lt
  Comparator comparator_12 (.a(register_1_q), .b(8'hc), .eq(comparator_12_eq));  // open: gt, lt
  Comparator comparator_13 (.a(register_1_q), .b(8'h10), .eq(comparator_13_eq));  // open: gt, lt
  Comparator comparator_14 (.a(register_1_q), .b(8'h11), .eq(comparator_14_eq));  // open: gt, lt
  Comparator comparator_15 (.a(register_1_q), .b(8'h12), .eq(comparator_15_eq));  // open: gt, lt
  Comparator comparator_16 (.a(register_1_q), .b(8'h13), .eq(comparator_16_eq));  // open: gt, lt
  Comparator comparator_17 (.a(register_1_q), .b(8'h14), .eq(comparator_17_eq));  // open: gt, lt
  Comparator comparator_18 (.a(register_1_q), .b(8'h15), .eq(comparator_18_eq));  // open: gt, lt
  Comparator comparator_19 (.a(register_1_q), .b(8'h16), .eq(comparator_19_eq));  // open: gt, lt
  Comparator comparator_20 (.a(register_1_q), .b(8'h17), .eq(comparator_20_eq));  // open: gt, lt
  Counter #(.trigger("falling")) counter_2 (
    .load(Jump), .D(Output), .count(not_1_out), .Q(counter_2_q), .clk(and_2_out), .clr(or_2_out));  // open: carry
  assign Adresse = not_2_out ? counter_2_q : 8'bz;  // Controlled_Buffer controlled_buffer_1
  not not_2 (not_2_out, counter_1_carry);
  or or_2 (or_2_out, Reset, and_4_out);
  Register #(.trigger("falling")) register_2 (.D(Input), .Q(Atribut), .clk(counter_1_q[0]), .clr(Reset));  // open: en
  nor nor_1 (nor_1_out, comparator_1_eq, comparator_2_eq, or_4_out, comparator_3_eq, comparator_4_eq);
  and and_3 (Write, or_3_out, Aufgabe);
  or or_3 (or_3_out, comparator_6_eq, comparator_7_eq, comparator_8_eq, comparator_9_eq, comparator_10_eq, comparator_11_eq, comparator_12_eq);
  or or_4 (or_4_out, comparator_5_eq, comparator_6_eq, or_5_out, comparator_7_eq, comparator_8_eq);
  or or_5 (or_5_out, comparator_9_eq, comparator_10_eq, or_6_out, comparator_11_eq, comparator_12_eq);
  or or_6 (or_6_out, comparator_13_eq, comparator_14_eq, or_7_out, comparator_15_eq, comparator_16_eq);
  or or_7 (or_7_out, comparator_17_eq, comparator_18_eq, comparator_19_eq, comparator_20_eq);
  and and_4 (and_4_out, Aufgabe, or_8_out);
  or or_8 (or_8_out, nor_1_out, comparator_14_eq);
  or or_9 (or_9_out, comparator_2_eq, comparator_3_eq);
  and and_5 (and_5_out, Aufgabe, comparator_8_eq);
  and and_6 (and_6_out, Aufgabe, comparator_13_eq);
  assign Output = and_6_out ? Atribut : 8'bz;  // Controlled_Buffer controlled_buffer_2
  and and_7 (and_7_out, Aufgabe, or_9_out);
  and and_8 (and_8_out, Aufgabe, or_10_out);
  or or_10 (or_10_out, comparator_4_eq, comparator_5_eq);
  assign Adresse = and_5_out ? Atribut : 8'bz;  // Controlled_Buffer controlled_buffer_3
  assign Output = and_5_out ? {8{1'b0}} : 8'bz;  // Controlled_Buffer controlled_buffer_4
  assign Adresse = and_7_out ? Atribut : 8'bz;  // Controlled_Buffer controlled_buffer_5
  assign Input_Speicher = and_7_out ? Input : 8'bz;  // Controlled_Buffer controlled_buffer_6
  assign Input_Speicher = and_8_out ? Atribut : 8'bz;  // Controlled_Buffer controlled_buffer_7
  assign Adresse = and_9_out ? Atribut : 8'bz;  // Controlled_Buffer controlled_buffer_8
  and and_9 (and_9_out, Aufgabe, comparator_6_eq);
  assign Output = and_9_out ? Speicher_A : 8'bz;  // Controlled_Buffer controlled_buffer_9
  assign Adresse = and_10_out ? Atribut : 8'bz;  // Controlled_Buffer controlled_buffer_10
  and and_10 (and_10_out, Aufgabe, comparator_7_eq);
  assign Output = and_10_out ? Speicher_B : 8'bz;  // Controlled_Buffer controlled_buffer_11
  Comparator comparator_21 (
    .a(Speicher_A), .b({8{1'b0}}), .gt(comparator_21_gt), .eq(comparator_21_eq), .lt(comparator_21_lt));
  Comparator comparator_22 (
    .a(Speicher_B), .b({8{1'b0}}), .gt(comparator_22_gt), .eq(comparator_22_eq), .lt(comparator_22_lt));
  and and_11 (and_11_out, Aufgabe, comparator_9_eq);
  and and_12 (and_12_out, Aufgabe, comparator_10_eq);
  and and_13 (and_13_out, Aufgabe, comparator_11_eq);
  and and_14 (and_14_out, Aufgabe, comparator_12_eq);
  and and_15 (and_15_out, ~comparator_21_gt, Aufgabe, comparator_15_eq);  // AND_Gate
  and and_16 (and_16_out, ~comparator_21_eq, Aufgabe, comparator_16_eq);  // AND_Gate
  and and_17 (and_17_out, ~comparator_21_lt, Aufgabe, comparator_17_eq);  // AND_Gate
  and and_18 (and_18_out, ~comparator_22_gt, Aufgabe, comparator_18_eq);  // AND_Gate
  and and_19 (and_19_out, ~comparator_22_eq, Aufgabe, comparator_19_eq);  // AND_Gate
  and and_20 (and_20_out, ~comparator_22_lt, Aufgabe, comparator_20_eq);  // AND_Gate
  or or_11 (or_11_out, comparator_3_eq, comparator_5_eq);
  or or_12 (or_12_out, and_11_out, and_12_out, and_13_out, and_14_out);
  Adder adder_1 (.a(Speicher_A), .b(Speicher_B), .out(adder_1_out));  // open: cin, cout
  assign Output = and_11_out ? adder_1_out : 8'bz;  // Controlled_Buffer controlled_buffer_12
  assign Output = and_12_out ? subtractor_1_out : 8'bz;  // Controlled_Buffer controlled_buffer_13
  Subtractor subtractor_1 (.a(Speicher_A), .b(Speicher_B), .out(subtractor_1_out));  // open: bin, bout
  Divider divider_1 (.a(Speicher_A), .b(Speicher_B), .out(divider_1_out));  // open: upper, rem
  assign Output = and_13_out ? divider_1_out : 8'bz;  // Controlled_Buffer controlled_buffer_14
  assign Output = and_14_out ? multiplier_1_out : 8'bz;  // Controlled_Buffer controlled_buffer_15
  Multiplier multiplier_1 (.a(Speicher_A), .b(Speicher_B), .out(multiplier_1_out));  // open: cin, cout
  and and_21 (and_21_out, Aufgabe, or_13_out);
  or or_13 (or_13_out, and_15_out, and_16_out, and_17_out, and_18_out, and_19_out, and_20_out);
  Register #(.trigger("high")) register_3 (
    .D(Input_Speicher), .Q(Speicher_A), .clk(and_22_out), .clr(or_2_out));  // open: en
  and and_22 (and_22_out, or_14_out, Aufgabe);
  or or_14 (or_14_out, comparator_2_eq, comparator_4_eq);
  Register #(.trigger("high")) register_4 (
    .D(Input_Speicher), .Q(Speicher_B), .clk(and_23_out), .clr(or_2_out));  // open: en
  and and_23 (and_23_out, or_11_out, Aufgabe);
  assign Adresse = or_12_out ? Atribut : 8'bz;  // Controlled_Buffer controlled_buffer_16
  or or_15 (Jump, and_6_out, and_21_out);
  assign Output = and_21_out ? Atribut : 8'bz;  // Controlled_Buffer controlled_buffer_17

  // Notes on the sheet:
  //   Nichts
  //   Lade von Ram [Input] zu A
  //   Lade von Ram [Input] zu B
  //   Lade von Input zu A
  //   Lade von Input zu B
  //   Speicher A zu Ram [Input]
  //   Speicher B zu Ram [Input]
  //   Speicher 0 zu Ram [Input]
  //   Lösche Ram [Input]
  //   A + B = Ram [Input]
  //   A - B = Ram [Input]
  //   A * B = Ram [Input]
  //   A / B = Ram [Input]
  //   Springe zu Input
  //   Reset
  //   If (A > 0) dann {Nichts} oder {gehe zu Input}
  //   If (A == 0) dann {Nichts} oder {gehe zu Input}
  //   If (A < 0) dann {Nichts} oder {gehe zu Input}
  //   If (B > 0) dann {Nichts} oder {gehe zu Input}
  //   If (B == 0) dann {Nichts} oder {gehe zu Input}
  //   If (B < 0) dann {Nichts} oder {gehe zu Input}
endmodule

module Mainbord (
  input  Reset,
  input  Aktive,
  input  [7:0] Ram_Output,
  input  CPU_Write,
  input  [7:0] CPU_Adresse,
  input  [7:0] CPU_Output,
  output Ram_Takt,
  output Ram_Schreibe,
  output [7:0] Ram_Input,
  output Ram_Aktive,
  output Ram_Lesen,
  output [7:0] Ram_Adresse,
  output \Ram_Löschen ,
  output CPU_Takt,
  output [7:0] CPU_Input,
  output CPU_Reset
);

  wire clock_1_out;

  and and_1 (CPU_Takt, Aktive, clock_1_out);
  Clock clock_1 (.out(clock_1_out));

  assign CPU_Input = Ram_Output;
  assign CPU_Reset = Reset;
  assign Ram_Adresse = CPU_Adresse;
  assign Ram_Aktive = 1'b1;
  assign Ram_Input = CPU_Output;
  assign Ram_Lesen = 1'b1;
  assign \Ram_Löschen  = 1'b0;
  assign Ram_Schreibe = CPU_Write;
  assign Ram_Takt = CPU_Takt;
endmodule
